// Logisim project UNIVERSAL SHIFT REGISTER.circ as structural Verilog: 1 circuit, main circuit main
module main (
  input  in_1,
  input  in_2,
  input  in_3,
  input  in_4,
  input  in_5,
  input  in_6,
  input  [1:0] in_7,
  input  in_8
);

  wire clock_1_out, d_ff_1_q, d_ff_2_q, d_ff_3_q, d_ff_4_q, multiplexer_1_out, multiplexer_2_out,
       multiplexer_3_out, multiplexer_4_out;

  Clock clock_1 (.out(clock_1_out));
  Multiplexer #(.select(2)) multiplexer_1 (
    .in0(d_ff_1_q), .in1(in_6), .in2(d_ff_2_q), .in3(in_1), .out(multiplexer_1_out), .sel(in_7));
  D_Flip_Flop d_ff_1 (.D(multiplexer_1_out), .clk(clock_1_out), .Q(d_ff_1_q), .reset(in_8));  // open: Qn, preset
  D_Flip_Flop d_ff_2 (.D(multiplexer_2_out), .clk(clock_1_out), .Q(d_ff_2_q), .reset(in_8));  // open: Qn, preset
  Multiplexer #(.select(2)) multiplexer_2 (
    .in0(d_ff_2_q), .in1(d_ff_1_q), .in2(d_ff_3_q), .in3(in_2), .out(multiplexer_2_out), .sel(in_7));
  Multiplexer #(.select(2)) multiplexer_3 (
    .in0(d_ff_3_q), .in1(d_ff_2_q), .in2(d_ff_4_q), .in3(in_3), .out(multiplexer_3_out), .sel(in_7));
  D_Flip_Flop d_ff_3 (.D(multiplexer_3_out), .clk(clock_1_out), .Q(d_ff_3_q), .reset(in_8));  // open: Qn, preset
  Multiplexer #(.select(2)) multiplexer_4 (
    .in0(d_ff_4_q), .in1(d_ff_3_q), .in2(in_5), .in3(in_4), .out(multiplexer_4_out), .sel(in_7));
  D_Flip_Flop d_ff_4 (.D(multiplexer_4_out), .clk(clock_1_out), .Q(d_ff_4_q), .reset(in_8));  // open: Qn, preset
endmodule
